# Fritzing sketch Reaction game (saved by Fritzing 0.9.9b)
circuit board: 8.46667cm x 5.64444cm
breadboards: 1

parts:
  Onderdeel1 = Arduino Uno (Rev3)
  S1 = Pushbutton [package="[THT]"]
  R1 = Resistor [tolerance=±5% power=0.25 resistance=220 package=THT]
  U1 = 74HC595 [package="DIP16 [THT]"]
  U2 = 7-SEGMENT-DISPLAY [package=7-segment-display]
  R2 = Resistor [tolerance=±5% power=0.25 resistance=220 package=THT]
  R3 = Resistor [tolerance=±5% power=0.25 resistance=220 package=THT]

nets:
  N1: Onderdeel1.D2, S1.Pin_3, S1.Pin_4
  N2: Onderdeel1.D3_PWM, U1.DS
  N3: Onderdeel1.D4, U1.ST_CP
  N4: Onderdeel1.D5_PWM, U1.SH_CP
  5V: Onderdeel1.5V, U1.MR, U1.VCC
  GND: Onderdeel1.GND, R1.Pin_0, U1.GND, U1.OE, R2.Pin_0, R3.Pin_1
  N5: S1.Pin_1, S1.Pin_2, R1.Pin_1
  N6: U1.Q1, U2.A
  N7: U1.Q2, U2.G2
  N8: U1.Q3, U2.G
  N9: U1.Q4, U2.E
  N10: U1.Q5, U2.G1
  N11: U1.Q6, U2.DP
  N12: U1.Q0, U2.D
  N13: U2.C, R3.Pin_0
  N14: U2.F, R2.Pin_1
